# Fritzing sketch DIGITALIO_74HC595_Graph (saved by Fritzing 0.8.3b)
circuit board: 8.46667cm x 5.64444cm
breadboards: 3

parts:
  U1 = 74HC595 [package="DIP16 [THT]"]
  D1 = LED_BARGRAPH_10 [package=led_bargaph_10]
  Bauteil1 = Arduino Uno (Rev3)
  R1 = Resistor [tolerance=±5% resistance=330 package=THT]
  R2 = Resistor [tolerance=±5% resistance=330 package=THT]
  R3 = Resistor [tolerance=±5% resistance=330 package=THT]
  R4 = Resistor [tolerance=±5% resistance=330 package=THT]
  R5 = Resistor [tolerance=±5% resistance=330 package=THT]
  R6 = Resistor [tolerance=±5% resistance=330 package=THT]
  R7 = Resistor [tolerance=±5% resistance=330 package=THT]
  R8 = Resistor [tolerance=±5% resistance=330 package=THT]

nets:
  N1: U1.Q1, R2.Pin_1
  N2: U1.Q2, R3.Pin_1
  N3: U1.Q3, R4.Pin_1
  N4: U1.Q4, R5.Pin_1
  N5: U1.Q5, R6.Pin_1
  N6: U1.Q6, R7.Pin_1
  N7: U1.Q7, R8.Pin_1
  GND: U1.GND, U1.OE, D1.J_C, D1.I_C, D1.H_C, D1.G_C, D1.F_C, D1.E_C, D1.D_C, D1.C_C, Bauteil1.GND
  VCC: U1.MR, U1.VCC, Bauteil1.5V
  N8: U1.SH_CP, Bauteil1.ICSP_MISO, Bauteil1.D12/MISO
  N9: U1.ST_CP, Bauteil1.D8
  N10: U1.DS, Bauteil1.ICSP_MOSI, Bauteil1.D11_PWM/MOSI
  N11: U1.Q0, R1.Pin_1
  N12: D1.C_A, R8.Pin_0
  N13: D1.D_A, R7.Pin_0
  N14: D1.E_A, R6.Pin_0
  N15: D1.F_A, R5.Pin_0
  N16: D1.G_A, R4.Pin_0
  N17: D1.H_A, R3.Pin_0
  N18: D1.I_A, R2.Pin_0
  N19: D1.J_A, R1.Pin_0

notes:
  /*
  Adafruit Arduino - Lesson 4. 8 LEDs and a Shift Register
  http://learn.adafruit.com/adafruit-arduino-lesson-4-eight-leds/arduino-code
  Shiftout tutorial
  http://arduino.cc/en/tutorial/ShiftOut
  PINS 1-7, 15 Q0 " Q7 Output Pins
  PIN 8 GND Ground, Vss
  PIN 9 Q7" Serial Out
  PIN 10 MR Master Reclear, active low
  PIN 11 SH_CP Shift register clock pin
  PIN 12 ST_CP Storage register clock pin (latch pin)
  PIN 13 OE Output enable, active low
  PIN 14 DS Serial data input
  PIN 16 Vcc Positive supply voltage
  */
  //Pin connected to ST_CP of 74HC595
  int latchPin = 8;
  //Pin connected to SH_CP of 74HC595
  int clockPin = 12;
  ////Pin connected to DS of 74HC595
  int dataPin = 11;
  byte leds = 0;
  void setup() {
  pinMode(latchPin, OUTPUT);
  pinMode(dataPin, OUTPUT);
  pinMode(clockPin, OUTPUT);
  setGraph(B10000111);
  // setBarGraph(0);
  // setBarGraphOf();
  }
  void loop(){
  //loopGraph();
  }
  void loopGraph(){
  leds = 0;
  updateShiftRegister();
  delay(500);
  for (int i = 0; i < 8; i++){
  bitSet(leds, i);
  updateShiftRegister();
  delay(500);
  }
  }
  void setGraph(byte val){
  digitalWrite(latchPin, LOW);
  shiftOut(dataPin, clockPin, LSBFIRST, val);
  digitalWrite(latchPin, HIGH);
  }
  void setBarGraphOf(){
  leds = 0;
  digitalWrite(latchPin, LOW);
  shiftOut(dataPin, clockPin, LSBFIRST, leds);
  digitalWrite(latchPin, HIGH);
  }
  void setBarGraph(int i){
  // leds = 0;
  bitSet(leds, i);
  digitalWrite(latchPin, LOW);
  shiftOut(dataPin, clockPin, LSBFIRST, leds);
  digitalWrite(latchPin, HIGH);
  }
  void updateShiftRegister(){
  digitalWrite(latchPin, LOW);
  shiftOut(dataPin, clockPin, LSBFIRST, leds);
  digitalWrite(latchPin, HIGH);
  }
